# Fritzing sketch ESP32s-Relay (saved by Fritzing 0.9.3b)
breadboards: 1

parts:
  KY-1 = Keyes Relay [package=THT]
  Mod1 = Elecrow ESP32S WiFi/BLE Board V1.0 [part_number=ARS01119B]
  R1 = Resistor [tolerance=±5% resistance=220 package=THT]
  LED1 = LED - 5mm [color="Red (633nm)" package="5 mm [THT]"]

nets:
  N1: KY-1.signal, Mod1.pin18
  N2: KY-1.power, KY-1.C, Mod1.pin38
  N3: KY-1.ground, Mod1.pin33, R1.Pin_0
  N4: KY-1.NO, LED1.anode
  N5: R1.Pin_1, LED1.cathode

custom parts:
  Keyes Relay: The Keyes 5V relay module is suitable for SCM development, home appliance control. It uses a 5V~12V TIL control signal which can control DC / AC signal.
  Elecrow ESP32S WiFi/BLE Board V1.0: The Elecrow ESP32S WiFi BLE Board V1.0 is one of the development boards created by Elecrow to evaluate the ESP-WROOM-32 module. It is based on the ESP32 microcontroller that boasts WiFi, Bluetooth, Ethernet and Low Power support all in a single chip. This board is 38 pins long (2x19) and 10 pins wide. Note in pcb view the mounting holes (2.8mm diameter) are only shown on silkscreen. If you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
